// Logisim project main.circ as structural Verilog: 3 circuits, main circuit main
module main (
);

  wire and_1_out, and_2_out, back, buttons_1_p6, cdm_16_1_p2, cdm_16_1_p6, check_collision, clock_2_out,
       collision, decoder_1_pixel_state__bit_8, decoder_1_write__bit_9, forward, game_over, left, memory,
       memory_map_extrude_1_map_active, not_1_out, not_2_out, ram_1_p4, read_write, right;
  wire [3:0] buttons_1_p5, decoder_1_x_coord__bits_0_3, decoder_1_y_coord__bits_4_7, keyboard,
       memory_map_extrude_1_out_4;
  wire [15:0] cdm_16_1_p1, cdm_16_1_p3, cdm_16_1_p7, cdm_16_1_p8, cdm_16_1_p9, controlled_buffer_2_out,
       display_controller_1_c00, display_controller_1_c01, display_controller_1_c02,
       display_controller_1_c03, display_controller_1_c04, display_controller_1_c05,
       display_controller_1_c06, display_controller_1_c07, display_controller_1_c08,
       display_controller_1_c09, display_controller_1_c10, display_controller_1_c11,
       display_controller_1_c12, display_controller_1_c13, display_controller_1_c14,
       display_controller_1_c15, multiplexer_1_out, s00, s01, s02, s03, s04, s05, s06, s07, s08, s09, s10,
       s11, s12, s13, s14, s15;

  // Debugger debugger_1: pin names not known
  // Probe on cdm_16_1_p1
  // CdM_16 cdm_16_1: pin names not known; wires that end beside it: cdm_16_1_p1, cdm_16_1_p2, {cdm_16_1_p3[15:3], game_over, check_collision, cdm_16_1_p3[0]}, memory, read_write, cdm_16_1_p6, cdm_16_1_p7, cdm_16_1_p8, cdm_16_1_p9
  decoder decoder_1 (
    .in_1(cdm_16_1_p1), .X_coord__bits_0_3(decoder_1_x_coord__bits_0_3),
    .Y_coord__bits_4_7(decoder_1_y_coord__bits_4_7), .pixel_state__bit_8(decoder_1_pixel_state__bit_8),
    .write__bit_9(decoder_1_write__bit_9));
  random_generator random_generator_1 (.get_random(cdm_16_1_p3[0]), .random_XY(s01));
  Clock clock_1 (.out(cdm_16_1_p2));
  DotMatrix #(.matrixcols(16), .matrixrows(16)) dotmatrix_1 (
    .col0(display_controller_1_c00), .col1(display_controller_1_c01), .col2(display_controller_1_c02),
    .col3(display_controller_1_c03), .col4(display_controller_1_c04), .col5(display_controller_1_c05),
    .col6(display_controller_1_c06), .col7(display_controller_1_c07), .col8(display_controller_1_c08),
    .col9(display_controller_1_c09), .col10(display_controller_1_c10), .col11(display_controller_1_c11),
    .col12(display_controller_1_c12), .col13(display_controller_1_c13), .col14(display_controller_1_c14),
    .col15(display_controller_1_c15));
  display_controller display_controller_1 (
    .X_coord(decoder_1_x_coord__bits_0_3), .Y_coord(decoder_1_y_coord__bits_4_7),
    .pixel_state(decoder_1_pixel_state__bit_8), .write(decoder_1_write__bit_9),
    .pixel_check(check_collision), .c01(display_controller_1_c01), .c02(display_controller_1_c02),
    .c03(display_controller_1_c03), .c04(display_controller_1_c04), .c05(display_controller_1_c05),
    .c06(display_controller_1_c06), .c07(display_controller_1_c07), .c08(display_controller_1_c08),
    .c09(display_controller_1_c09), .c10(display_controller_1_c10), .c11(display_controller_1_c11),
    .c12(display_controller_1_c12), .c13(display_controller_1_c13), .c14(display_controller_1_c14),
    .c15(display_controller_1_c15), .checked(collision), .game_over(game_over), .c00(display_controller_1_c00));  // open: victory, req_rand, food
  Button button (.out(forward));
  Button button_2 (.out(left));
  Button button_3 (.out(back));
  assign cdm_16_1_p9 = read_write ? controlled_buffer_2_out : 16'bz;  // Controlled_Buffer controlled_buffer_1
  Button button_4 (.out(right));
  assign controlled_buffer_2_out = not_1_out ? cdm_16_1_p8 : 16'bz;  // Controlled_Buffer controlled_buffer_2
  not not_1 (not_1_out, read_write);
  // Probe on cdm_16_1_p7
  // Buttons buttons_1: pin names not known; wires that end beside it: forward, right, back, left, buttons_1_p5, buttons_1_p6
  // Probe on cdm_16_1_p7
  and and_1 (and_1_out, memory, not_2_out);
  Clock clock_2 (.out(clock_2_out));
  Register #(.width(4)) register_1 (.D(buttons_1_p5), .Q(keyboard), .clk(buttons_1_p6));  // open: en, clr
  // RAM ram_1: pin names not known; wires that end beside it: cdm_16_1_p7, cdm_16_1_p6, and_1_out, ram_1_p4, read_write, controlled_buffer_2_out
  Clock clock_3 (.out(ram_1_p4));
  not not_2 (not_2_out, and_2_out);
  and and_2 (and_2_out, read_write, clock_2_out, memory_map_extrude_1_map_active);
  memory_map_extrude memory_map_extrude_1 (
    .addr(cdm_16_1_p7), .constant(12'h880), .out_4(memory_map_extrude_1_out_4),
    .map_active(memory_map_extrude_1_map_active));
  Multiplexer #(.select(4), .width(16)) multiplexer_1 (
    .in0(s00), .in1(s01), .in2(s02), .in3(s03), .in4(s04), .in5(s05), .in6(s06), .in7(s07), .in8(s08),
    .in9(s09), .in10(s10), .in11(s11), .in12(s12), .in13(s13), .in14(s14), .in15(s15),
    .out(multiplexer_1_out), .sel(memory_map_extrude_1_out_4), .en(1'b1));
  assign controlled_buffer_2_out = and_2_out ? multiplexer_1_out : 16'bz;  // Controlled_Buffer controlled_buffer_3
  assign s02 = {{15{1'b0}}, collision};  // Bit_Extender bit_extender_1
  assign s00 = {{12{1'b0}}, keyboard};  // Bit_Extender bit_extender_2

  // Notes on the sheet:
  //   Тут мы ставим кнопки для управления змеёй
  //   Тут мы ставим счётчик
endmodule

module memory_map_extrude (
  input  [15:0] addr,
  input  [11:0] constant,
  output map_active,
  output [3:0] out_4
);

  wire and_1_out, and_2_out, and_4_out, and_5_out;
  wire [11:0] xnor_1_out;

  assign xnor_1_out = ~(addr[15:4] ^ constant);  // XNOR_Gate xnor_1, 12 bits wide
  and and_1 (and_1_out, xnor_1_out[8], xnor_1_out[7], xnor_1_out[6]);
  and and_2 (and_2_out, xnor_1_out[11], xnor_1_out[10], xnor_1_out[9]);
  and and_3 (map_active, and_2_out, and_1_out, and_5_out, and_4_out);
  and and_4 (and_4_out, xnor_1_out[2], xnor_1_out[1], xnor_1_out[0]);
  and and_5 (and_5_out, xnor_1_out[5], xnor_1_out[4], xnor_1_out[3]);

  assign out_4 = addr[3:0];
endmodule

module random_generator (
  input  get_random,
  output [15:0] random_XY
);

  wire [7:0] random_1_out;

  Random #(.trigger("falling")) random_1 (.clk(get_random), .out(random_1_out));  // open: next, clr
  assign random_XY = {{8{1'b0}}, random_1_out};  // Bit_Extender bit_extender_1
endmodule
